# Fritzing sketch esquemaCartelTirasLED (saved by Fritzing 0.9.6b)

parts:
  Part1 = Arduino Uno (Rev3) - ICSP
  U1 = WS2812 RGB LED strip
  U2 = WS2812 RGB LED strip
  C1 = Capacitor Polarized [package=cpol-radial-1000uf-25v]
  VCC1 = Battery  # not connected
  R1 = Resistor [tolerance=±5% resistance=470 package="0603 [SMD]"]

nets:
  N1: Part1.GND, U1.GND#0, C1.+
  N2: Part1.D6_PWM, R1.Pin_0
  N3: Part1.5V, U1.VCC#1
  N4: Part1.VIN, C1.-
  N5: U1.GND#4, U2.GND
  N6: U1.VCC#5, U2.VCC
  N7: U1.DOUT, U2.DIN

custom parts:
  WS2812 RGB LED strip: WS2812 strip
  Battery: Your standard 2x 18650 battery pack (7,4 Volts)
